// Logisim project part3.circ as structural Verilog: 6 circuits, main circuit main
module main (
  input  X
);

  wire clock_1_out, logicgates_1_a, logicgates_1_b, logicgates_1_c, logicgates_1_d, logicgates_1_e,
       logicgates_1_f, logicgates_1_g, logicgates_2_a, logicgates_2_b, logicgates_2_c, logicgates_2_d,
       logicgates_2_e, logicgates_2_f, logicgates_2_g, n6bitcounter_1__1, n6bitcounter_1__2,
       n6bitcounter_1__4, n6bitcounter_1_out_6, n10bitcounter_1__1, n10bitcounter_1__2, n10bitcounter_1__4,
       n10bitcounter_1__8, n10bitcounter_1_isnine_zero;

  Clock clock_1 (.out(clock_1_out));
  _10bitcounter u_10bitcounter_1 (
    .X(X), .Clock(clock_1_out), .IsNine_Zero(n10bitcounter_1_isnine_zero), ._1(n10bitcounter_1__1),
    ._2(n10bitcounter_1__2), ._4(n10bitcounter_1__4), ._8(n10bitcounter_1__8));
  _6bitcounter u_6bitcounter_1 (
    .Clock(n10bitcounter_1_isnine_zero), .X(X), ._1(n6bitcounter_1__1), ._2(n6bitcounter_1__2),
    ._4(n6bitcounter_1__4), .out_6(n6bitcounter_1_out_6));
  logicgates logicgates_1 (
    .W(n10bitcounter_1__8), .X(n10bitcounter_1__4), .Y(n10bitcounter_1__2), .Z(n10bitcounter_1__1),
    .g(logicgates_1_g), .d(logicgates_1_d), .a(logicgates_1_a), .b(logicgates_1_b), .f(logicgates_1_f),
    .e(logicgates_1_e), .c(logicgates_1_c));
  _7_Segment_Display u_7_segment_display_1 (
    .g(logicgates_2_g), .f(logicgates_2_f), .a(logicgates_2_a), .b(logicgates_2_b), .e(logicgates_2_e),
    .d(logicgates_2_d), .c(logicgates_2_c));  // open: dp
  logicgates logicgates_2 (
    .W(n6bitcounter_1_out_6), .X(n6bitcounter_1__4), .Y(n6bitcounter_1__2), .Z(n6bitcounter_1__1),
    .g(logicgates_2_g), .d(logicgates_2_d), .a(logicgates_2_a), .b(logicgates_2_b), .f(logicgates_2_f),
    .e(logicgates_2_e), .c(logicgates_2_c));
  _7_Segment_Display u_7_segment_display_2 (
    .g(logicgates_1_g), .f(logicgates_1_f), .a(logicgates_1_a), .b(logicgates_1_b), .e(logicgates_1_e),
    .d(logicgates_1_d), .c(logicgates_1_c));  // open: dp
endmodule

module dec_counter (
  input  Clock,
  output _3,
  output _2,
  output _1,
  output _0,
  output isNine
);

  wire and_1_out, and_2_out, and_3_out, and_4_out, and_5_out, and_6_out, and_7_out, D1_qn, D2_qn, D3_qn,
       D4_qn, or_1_out, or_2_out, or_3_out;

  and and_1 (and_1_out, _3, D4_qn);
  and and_2 (and_2_out, _1, _0, _2);
  and and_3 (and_3_out, _2, D3_qn);
  and and_4 (and_4_out, _2, D4_qn);
  and and_5 (and_5_out, _1, _0, D2_qn);
  and and_6 (and_6_out, _1, D4_qn);
  and and_7 (and_7_out, D3_qn, D1_qn, _0);
  or or_1 (or_1_out, and_1_out, and_2_out);
  or or_2 (or_2_out, and_3_out, and_4_out, and_5_out);
  or or_3 (or_3_out, and_6_out, and_7_out);
  D_Flip_Flop #(.trigger("falling")) D1 (.clk(Clock), .D(or_1_out), .Q(_3), .Qn(D1_qn));  // open: preset, en, reset
  D_Flip_Flop #(.trigger("falling")) D2 (.clk(Clock), .D(or_2_out), .Q(_2), .Qn(D2_qn));  // open: preset, en, reset
  D_Flip_Flop #(.trigger("falling")) D3 (.clk(Clock), .D(or_3_out), .Q(_1), .Qn(D3_qn));  // open: preset, en, reset
  D_Flip_Flop #(.trigger("falling")) D4 (.clk(Clock), .D(D4_qn), .Q(_0), .Qn(D4_qn));  // open: preset, en, reset
  and and_8 (isNine, _0, D3_qn, D2_qn, _3);
endmodule

module logicgates (
  input  W,
  input  X,
  input  Y,
  input  Z,
  output g,
  output d,
  output a,
  output b,
  output f,
  output e,
  output c
);

  wire and_1_out, and_2_out, and_3_out, and_4_out, and_5_out, and_6_out, and_7_out, and_8_out, and_9_out,
       and_10_out, not_1_out, not_3_out, not_4_out, xnor_1_out, xnor_2_out;

  not not_1 (not_1_out, Z);
  // NOT_Gate not_2 has open pins: in=W, out=open
  not not_3 (not_3_out, X);
  not not_4 (not_4_out, Y);
  and and_1 (and_1_out, not_1_out, Y);
  and and_2 (and_2_out, Y, not_3_out);
  and and_3 (and_3_out, X, not_4_out);
  and and_4 (and_4_out, not_3_out, Y);
  and and_5 (and_5_out, Y, not_1_out);
  and and_6 (and_6_out, not_4_out, Z, X);
  and and_7 (and_7_out, not_1_out, not_3_out);
  xnor xnor_1 (xnor_1_out, X, Z);
  xnor xnor_2 (xnor_2_out, Z, Y);
  and and_8 (and_8_out, not_1_out, not_4_out);
  and and_9 (and_9_out, not_3_out, not_1_out);
  and and_10 (and_10_out, Y, not_1_out);
  or or_1 (c, not_4_out, Z, X);
  or or_2 (g, W, and_1_out, and_2_out, and_3_out);
  or or_3 (d, and_4_out, and_5_out, and_6_out, and_7_out);
  or or_4 (a, xnor_1_out, Y, W);
  or or_5 (b, xnor_2_out, not_3_out);
  or or_6 (f, W, and_8_out, X);
  or or_7 (e, and_9_out, and_10_out);
endmodule

module _10bitcounter (
  input  X,
  input  Clock,
  output _1,
  output _2,
  output _4,
  output _8,
  output IsNine_Zero
);

  wire and_1_out, and_2_out, and_3_out, and_4_out, and_5_out, and_6_out, and_7_out, and_8_out, and_9_out,
       and_10_out, j_k_ff_1_qn, j_k_ff_2_qn, j_k_ff_3_qn, j_k_ff_4_qn, not_1_out, not_2_out, not_3_out,
       not_4_out, not_5_out, not_6_out, not_7_out, not_8_out, not_9_out, not_10_out, not_11_out, not_12_out,
       not_13_out, or_1_out, or_2_out, or_3_out, or_4_out, or_5_out, xor_1_out, xor_2_out;

  xor xor_1 (xor_1_out, X, _1);
  J_K_Flip_Flop j_k_ff_1 (
    .J(or_2_out), .clk(Clock), .K(xor_1_out), .Q(_8), .Qn(j_k_ff_1_qn));  // open: preset, en, reset
  or or_1 (or_1_out, and_3_out, and_4_out);
  or or_2 (or_2_out, and_1_out, and_2_out);
  or or_3 (or_3_out, and_5_out, and_6_out);
  and and_1 (and_1_out, not_1_out, _2, _4, _1);
  and and_2 (and_2_out, not_2_out, X, not_3_out, not_4_out);
  and and_3 (and_3_out, _2, _1, not_5_out);
  and and_4 (and_4_out, X, _8, not_6_out);
  and and_5 (and_5_out, not_7_out, _2, _1);
  and and_6 (and_6_out, not_8_out, X, not_9_out);
  not not_1 (not_1_out, X);
  not not_2 (not_2_out, _4);
  not not_3 (not_3_out, _2);
  not not_4 (not_4_out, _1);
  J_K_Flip_Flop j_k_ff_2 (
    .J(or_1_out), .clk(Clock), .K(or_3_out), .Q(_4), .Qn(j_k_ff_2_qn));  // open: preset, en, reset
  not not_5 (not_5_out, X);
  not not_6 (not_6_out, _1);
  not not_7 (not_7_out, X);
  not not_8 (not_8_out, _1);
  not not_9 (not_9_out, _2);
  xor xor_2 (xor_2_out, X, _1);
  J_K_Flip_Flop j_k_ff_3 (
    .J(or_4_out), .clk(Clock), .K(xor_2_out), .Q(_2), .Qn(j_k_ff_3_qn));  // open: preset, en, reset
  or or_4 (or_4_out, and_7_out, and_8_out);
  and and_7 (and_7_out, or_5_out, X, not_10_out);
  and and_8 (and_8_out, _1, not_11_out, not_12_out);
  not not_10 (not_10_out, _1);
  not not_11 (not_11_out, X);
  not not_12 (not_12_out, _8);
  J_K_Flip_Flop j_k_ff_4 (.J(1'b1), .clk(Clock), .K(1'b1), .Q(_1), .Qn(j_k_ff_4_qn));  // open: preset, en, reset
  or or_5 (or_5_out, _4, _8);
  and and_9 (and_9_out, j_k_ff_3_qn, _8, X, j_k_ff_2_qn, _1);
  not not_13 (not_13_out, X);
  and and_10 (and_10_out, j_k_ff_1_qn, j_k_ff_4_qn, j_k_ff_3_qn, j_k_ff_2_qn, not_13_out);
  or or_6 (IsNine_Zero, and_9_out, and_10_out);
endmodule

module _6bitcounter (
  input  Clock,
  input  X,
  output _1,
  output _2,
  output _4,
  output out_6
);

  wire and_1_out, and_2_out, and_3_out, and_4_out, and_5_out, and_6_out, and_7_out, and_8_out, d_ff_1_qn,
       d_ff_2_qn, d_ff_3_qn, not_1_out, or_1_out, or_2_out, or_3_out, or_4_out, or_5_out, or_6_out;

  or or_1 (or_1_out, or_2_out, or_3_out);
  or or_2 (or_2_out, and_1_out, and_2_out);
  or or_3 (or_3_out, and_3_out, and_4_out);
  or or_4 (or_4_out, or_6_out, or_5_out);
  and and_1 (and_1_out, _2, not_1_out, _1);
  and and_2 (and_2_out, _4, not_1_out, d_ff_3_qn);
  and and_3 (and_3_out, _1, _4, X);
  and and_4 (and_4_out, d_ff_1_qn, d_ff_2_qn, d_ff_3_qn, X);
  or or_5 (or_5_out, and_5_out, and_6_out);
  D_Flip_Flop d_ff_1 (.clk(Clock), .D(or_1_out), .Q(_4), .Qn(d_ff_1_qn));  // open: preset, en, reset
  or or_6 (or_6_out, and_7_out, and_8_out);
  and and_5 (and_5_out, _1, _2, X);
  and and_6 (and_6_out, d_ff_3_qn, _4, X);
  D_Flip_Flop d_ff_2 (.clk(Clock), .D(or_4_out), .Q(_2), .Qn(d_ff_2_qn));  // open: preset, en, reset
  and and_7 (and_7_out, d_ff_3_qn, _2, not_1_out);
  and and_8 (and_8_out, _1, not_1_out, d_ff_2_qn, d_ff_1_qn);
  D_Flip_Flop d_ff_3 (.clk(Clock), .D(d_ff_3_qn), .Q(_1), .Qn(d_ff_3_qn));  // open: preset, en, reset
  not not_1 (not_1_out, X);

  assign out_6 = 1'b0;
endmodule

module _6bittest (
  input  Clock,
  output _1,
  output _2,
  output _4
);

  wire and_1_out, and_2_out, and_3_out, and_4_out, d_ff_1_qn, d_ff_2_qn, d_ff_3_qn, or_1_out, or_2_out;

  or or_1 (or_1_out, and_1_out, and_2_out);
  and and_1 (and_1_out, _2, _1);
  and and_2 (and_2_out, _4, d_ff_3_qn);
  or or_2 (or_2_out, and_3_out, and_4_out);
  D_Flip_Flop d_ff_1 (.clk(Clock), .D(or_1_out), .Q(_4), .Qn(d_ff_1_qn));  // open: preset, en, reset
  and and_3 (and_3_out, d_ff_3_qn, _2);
  and and_4 (and_4_out, _1, d_ff_2_qn, d_ff_1_qn);
  D_Flip_Flop d_ff_2 (.clk(Clock), .D(or_2_out), .Q(_2), .Qn(d_ff_2_qn));  // open: preset, en, reset
  D_Flip_Flop d_ff_3 (.clk(Clock), .D(d_ff_3_qn), .Q(_1), .Qn(d_ff_3_qn));  // open: preset, en, reset
endmodule
